// Logisim project simulation.circ as structural Verilog: 1 circuit, main circuit main
module main (
  input  MENU,
  input  nRD,
  input  nWR
);

  wire clock_1_out, nand_1_out, nand_2_out, nand_3_out, nand_4_out, nand_5_out, nand_6_out, nor_1_out,
       nor_2_out, nor_3_out, nor_4_out, nor_5_out, not_1_out, or_1_out, or_2_out, or_3_out, or_4_out;
  wire [7:0] register_1_q;

  Clock #(.highDuration(4)) clock_1 (.out(clock_1_out));
  or or_1 (or_1_out, MENU, clock_1_out);
  Register register_1 (.Q(register_1_q));  // open: D, en, clk, clr
  nand nand_1 (nand_1_out, or_1_out, or_2_out);
  or or_2 (or_2_out, nand_2_out, not_1_out);
  nand nand_2 (nand_2_out, MENU, MENU);
  nand nand_3 (nand_3_out, nand_1_out, nand_1_out);
  or or_3 (or_3_out, register_1_q[6], nWR);
  not not_1 (not_1_out, nand_4_out);
  nand nand_4 (nand_4_out, or_3_out, nRD);
  nand nand_5 (nand_5_out, MENU, not_1_out);
  or or_4 (or_4_out, register_1_q[5], nRD);
  nand nand_6 (nand_6_out, MENU, MENU);
  nor nor_1 (nor_1_out, MENU, clock_1_out);
  nor nor_2 (nor_2_out, nand_6_out, not_1_out);
  nor nor_3 (nor_3_out, nand_6_out, nand_4_out);
  nor nor_4 (nor_4_out, nor_1_out, nor_2_out);
  nor nor_5 (nor_5_out, nor_3_out, nor_3_out);

  // Notes on the sheet:
  //   #PSEN
  //   Port P1
  //   "CS"
  //   #RAM_CS
  //   #WR
  //   "#CS"
  //   #ROM_OE
endmodule
